# Fritzing sketch Smart pot -small(폐기) (saved by Fritzing 0.9.3b)
breadboards: 1

parts:
  부품1 = LCD1602-I2C
  Part1 = KY-015 Temperature & Humidity Sensor Module [package="Breakout board"]
  WATER_PUMP1 = water pump/motor
  부품2 = FC-28 Soil Hygrometer Module - Probe
  Q1 = Basic FET N-Channel [part_number=IRFZ44n package="TO220 [THT]"]
  LED1 = RGB LED (com. cathode, rgb) [package="5 mm [THT]"]
  U1 = Voltage Regulator - 5V [package="TO220 [THT]"]
  C1 = Capacitor Polarized [package=cpol-radial-1000uf-25v]
  C2 = Capacitor [package=cap-pth-small2]
  VCC1 = Battery block 9V
  F1 = Resettable Fuse PTC [package=ptc]
  D2 = Rectifier Diode [part_number=1N4001 package="300 mil [THT]"]
  U2 = atmega328 [package=dip]
  S1 = Pushbutton [package="[SMD]"]
  R1 = Resistor [tolerance=±5% resistance=10k package=THT]
  D3 = Rectifier Diode [part_number=1N4001 package="300 mil [THT]"]
  C3 = Capacitor [package=cap-pth-small2]
  LED2 = LED - 5mm [color="Green (560nm)" package="5 mm [THT]"]
  R3 = Resistor [tolerance=±5% resistance=150 package=THT]
  LED3 = LED - 5mm [color="Orange (612nm)" package="5 mm [THT]"]
  C4_18pf = Ceramic Capacitor [capacitance=100nF package="100 mil [THT, multilayer]"]
  C4_18pf1 = Ceramic Capacitor [capacitance=100nF package="100 mil [THT, multilayer]"]
  C4 = Ceramic Capacitor [capacitance=100nF package="100 mil [THT, multilayer]"]
  C5 = Ceramic Capacitor [capacitance=100nF package="100 mil [THT, multilayer]"]
  R4 = Resistor [tolerance=±5% resistance=150 package=THT]
  D18 = Schottky Diode [part_number=1N5817 package="300 mil [THT]"]
  C6 = Capacitor Polarized [package=cpol-radial-100uf-25v]
  R5 = Resistor [tolerance=±5% resistance=220 package=THT]
  R6 = Resistor [tolerance=±5% resistance=220 package=THT]
  BT1 = Bluetooth HC-06u [package=THT]
  R7 = Resistor [tolerance=±5% resistance=10k package=THT]
  R2 = Resistor [tolerance=±5% resistance=150 package=THT]
  XTAL1 = Crystal [frequency="16 Mhz" package=THT]

nets (from the schematic view):
  GND: 부품1.GND, Part1.-, Q1.source, U1.GND, C1.-, C2.2, VCC1.-, S1.Pin_3, S1.Pin_4, C3.1, LED2.cathode, LED3.cathode, C4_18pf.1, C4_18pf1.1, R4.Pin_1, D18.anode, C6.-, R5.Pin_0, BT1.GND, R7.Pin_0
  5V: 부품1.VCC, Part1.Vin, WATER_PUMP1.pin_1, 부품2.POS, U1.output_voltage, C1.+, C2.1, R1.Pin_1, D3.cathode, R3.Pin_1, BT1.VCC, R2.Pin_1
  SDA: 부품1.SDA, U2.A4
  SCK: 부품1.SCL, U2.A5
  A1: Part1.S, U2.A1
  N1: WATER_PUMP1.pin_2, Q1.drain, D18.cathode
  A0: 부품2.NEG, U2.A0, R7.Pin_1
  N2: Q1.gate, R5.Pin_1, R6.Pin_1
  D5: LED1.red_anode, U2.D5_(PWM)
  N3: LED1.common_cathode, R4.Pin_0
  D6: LED1.green_anode, U2.D6_(PWM)
  D7: LED1.blue_anode, U2.D7
  N4: U1.input_voltage, D2.cathode, C6.+
  N5: VCC1.+, F1.1
  N6: F1.2, D2.anode
  RESET: U2.RESET, S1.Pin_1, S1.Pin_2, R1.Pin_0, D3.anode, C3.2
  N7: U2.VCC, C4.1
  N8: U2.GND#7, C4.0
  N9: U2.XLAT1, C4_18pf1.0, XTAL1.pin_0
  N10: U2.XLAT2, C4_18pf.0, XTAL1.pin_1
  D8: U2.D8, R6.Pin_0
  D10: U2.D10_(PWM), BT1.TXD
  D11: U2.D11_(PWM), BT1.RXD
  D13: U2.D13, R3.Pin_0, LED3.anode
  N11: U2.AVCC, C5.0
  N12: U2.GND#21, C5.1
  N13: LED2.anode, R2.Pin_0

notes:
  Arduino SmartPot

custom parts:
  LCD1602-I2C: A standard character display, usually with 2x16 characters. Comes in many colors with LCM1602 IIC attached.
  KY-015 Temperature & Humidity Sensor Module: KY-015 temperature and humidity sensor module, provides a low-latency serial interface to measure humidity and temperature.
  water pump/motor: WATER PUMP BY ARDUBLOCKTR
  FC-28 Soil Hygrometer Module - Probe: The FC-28 is a soil hygrometer module that uses the Texas Instruments LM393 comparator chip to provide an analog measurement of soil humidity.
  Bluetooth HC-06u: Bluetooth HC-06 - face up, pins down 16.5mm x 37.5mm PCB
