# Fritzing sketch Smart pot (saved by Fritzing 0.9.3b)
breadboards: 1

parts:
  부품1 = LCD1602-I2C
  Part1 = KY-015 Temperature & Humidity Sensor Module [package="Breakout board"]
  BT1 = Bluetooth HC-06u [package=THT]
  WATER_PUMP1 = water pump/motor  # not connected
  부품2 = FC-28 Soil Hygrometer Module - Probe
  부품3 = Arduino Uno (Rev3)
  Q1 = Basic FET N-Channel [part_number=IRFZ44n package="TO220 [THT]"]
  LED1 = RGB LED (com. cathode, rgb) [package="5 mm [THT]"]
  R2 = Resistor [tolerance=±5% resistance=220 package=THT]
  R3 = Resistor [tolerance=±5% resistance=220 package=THT]
  D1 = Rectifier Diode [part_number=1N4001 package="300 mil [THT]"]
  R4 = Resistor [tolerance=±5% resistance=100k package=THT]
  R5 = Resistor [tolerance=±5% resistance=150 package=THT]
  C1 = Capacitor [package=cap-pth-small2]
  C2_220uf = Electrolytic Capacitor [capacitance=22µF package="200 mil [THT, electrolytic]"]
  C3 = Capacitor Polarized [package=cpol-radial-1000uf-25v]
  U1 = Voltage Regulator - 5V [package="TO220 [THT]"]

nets:
  GND: 부품1.GND, Part1.-, BT1.GND, 부품3.GND, Q1.source, R3.Pin_0, D1.anode, R4.Pin_0, R5.Pin_1, C1.2, C2_220uf.-, C3.-, U1.GND
  VCC: 부품1.VCC, Part1.Vin, BT1.VCC, 부품2.POS, 부품3.5V, C2_220uf.+
  N1: 부품1.SDA, 부품3.A4/SDA
  N2: 부품1.SCL, 부품3.A5/SCL
  N3: Part1.S, 부품3.A1
  N4: BT1.TXD, 부품3.D10_PWM/SS
  N5: BT1.RXD, 부품3.D11_PWM/MOSI
  N6: 부품2.NEG, 부품3.A0, R4.Pin_1
  N7: 부품3.D8, R2.Pin_0, R3.Pin_1
  N8: 부품3.D5_PWM, LED1.red_anode
  N9: 부품3.D6_PWM, LED1.green_anode
  N10: 부품3.D7, LED1.blue_anode
  N11: 부품3.VIN, U1.input_voltage
  N12: Q1.gate, R2.Pin_1
  N13: Q1.drain, D1.cathode
  N14: LED1.common_cathode, R5.Pin_0
  N15: C1.1, C3.+, U1.output_voltage

custom parts:
  LCD1602-I2C: A standard character display, usually with 2x16 characters. Comes in many colors with LCM1602 IIC attached.
  KY-015 Temperature & Humidity Sensor Module: KY-015 temperature and humidity sensor module, provides a low-latency serial interface to measure humidity and temperature.
  Bluetooth HC-06u: Bluetooth HC-06 - face up, pins down 16.5mm x 37.5mm PCB
  water pump/motor: WATER PUMP BY ARDUBLOCKTR
  FC-28 Soil Hygrometer Module - Probe: The FC-28 is a soil hygrometer module that uses the Texas Instruments LM393 comparator chip to provide an analog measurement of soil humidity.
